// Logisim project FourBitParity.circ as structural Verilog: 3 circuits, main circuit implementation
module implementation (
  input  EnableIn,
  input  InputBitIn,
  input  ClkIn,
  output IsEvenOut
);

  wire [2:0] nextstate_1_nextstate, register_1_q;

  // Probe on register_1_q
  // Probe on nextstate_1_nextstate
  Register #(.width(3)) register_1 (.D(nextstate_1_nextstate), .clk(ClkIn), .Q(register_1_q));  // open: en, clr
  NextState nextstate_1 (.STATE(register_1_q), .INPUT(InputBitIn), .NextState(nextstate_1_nextstate));
  OutputEqn outputeqn_1 (.NextState(register_1_q), .Output(IsEvenOut));

  // Other names for the same wires on the sheet: Clk = ClkIn; Enable = EnableIn; InputBit = InputBitIn
endmodule

module NextState (
  input  [2:0] STATE,
  input  INPUT,
  output [2:0] NextState
);

  wire and_1_out, and_2_out, and_3_out, and_4_out, and_5_out, and_6_out, and_7_out, not_1_out, not_3_out,
       not_4_out;

  not not_1 (not_1_out, STATE[2]);
  not not_2 (NextState[1], STATE[1]);
  not not_3 (not_3_out, STATE[0]);
  not not_4 (not_4_out, INPUT);
  and and_1 (and_1_out, not_1_out, NextState[1], INPUT);
  and and_2 (and_2_out, NextState[1], STATE[0], INPUT);
  and and_3 (and_3_out, STATE[1], not_3_out);
  and and_4 (and_4_out, STATE[2], not_3_out, not_4_out);
  and and_5 (and_5_out, not_1_out, STATE[1], INPUT);
  and and_6 (and_6_out, STATE[2], NextState[1]);
  and and_7 (and_7_out, STATE[2], not_4_out);
  or or_1 (NextState[2], and_1_out, and_2_out, and_3_out, and_4_out);
  or or_2 (NextState[0], and_5_out, and_6_out, and_7_out);
endmodule

module OutputEqn (
  input  [2:0] NextState,
  output Output
);

  wire not_1_out, not_2_out;

  not not_1 (not_1_out, NextState[2]);
  not not_2 (not_2_out, NextState[1]);
  and and_1 (Output, not_1_out, not_2_out, NextState[0]);
endmodule
