// Logisim project UpDownCounter.circ as structural Verilog: 2 circuits, main circuit implementation
module implementation (
  input  EnableIn,
  input  CountUpIn,
  input  CountDownIn,
  input  clkIn,
  output [2:0] Count
);

  wire [2:0] nextstatecirc_1_nextstate;

  NextStateCirc nextstatecirc_1 (
    .State(Count), .Up(CountUpIn), .Down(CountDownIn), .NextState(nextstatecirc_1_nextstate));
  // Probe on nextstatecirc_1_nextstate
  Register #(.width(3)) register_1 (.D(nextstatecirc_1_nextstate), .en(EnableIn), .clk(clkIn), .Q(Count));  // open: clr
  // Probe on Count

  // Other names for the same wires on the sheet: clk = clkIn; CountDown = CountDownIn; CountUp = CountUpIn;
  //   Enable = EnableIn
endmodule

module NextStateCirc (
  input  [2:0] State,
  input  Up,
  input  Down,
  output [2:0] NextState
);

  wire and_1_out, and_2_out, and_3_out, and_4_out, and_5_out, and_6_out, and_7_out, and_8_out, and_9_out,
       and_10_out, and_11_out, and_12_out, and_13_out, and_14_out, not_1_out, not_2_out, not_3_out, not_4_out;

  not not_1 (not_1_out, State[1]);
  not not_2 (not_2_out, State[0]);
  not not_3 (not_3_out, Up);
  not not_4 (not_4_out, Down);
  and and_1 (and_1_out, State[1], State[0], Up);
  and and_2 (and_2_out, State[2], not_4_out);
  and and_3 (and_3_out, State[2], State[0]);
  and and_4 (and_4_out, State[2], State[1], not_3_out);
  and and_5 (and_5_out, not_1_out, State[0], Up);
  and and_6 (and_6_out, State[1], not_2_out, not_4_out);
  and and_7 (and_7_out, State[1], State[0], not_3_out);
  and and_8 (and_8_out, State[2], not_1_out, not_2_out, Down);
  and and_9 (and_9_out, State[2], State[1], not_4_out);
  and and_10 (and_10_out, not_2_out, Up);
  and and_11 (and_11_out, State[0], not_3_out, not_4_out);
  and and_12 (and_12_out, State[1], not_2_out, Down);
  and and_13 (and_13_out, State[2], not_2_out, Down);
  and and_14 (and_14_out, State[2], State[1], Up);
  or or_1 (NextState[2], and_1_out, and_2_out, and_3_out, and_4_out);
  or or_2 (NextState[1], and_5_out, and_6_out, and_7_out, and_8_out, and_9_out);
  or or_3 (NextState[0], and_10_out, and_11_out, and_12_out, and_13_out, and_14_out);
endmodule
