// Logisim project Vending.circ as structural Verilog: 2 circuits, main circuit implementation
module implementation (
  input  EnableIn,
  input  QuarterReceivedIn,
  input  DimeReceivedIn,
  input  NickelReceivedIn,
  input  ClkIn,
  output Give_Mechandise_Out,
  output Give_Dime_Out,
  output Give_Nickel_Out
);


  // Other names for the same wires on the sheet: clk = ClkIn; DimeReceieved = DimeReceivedIn; Enable = EnableIn;
  //   Give_Dime = Give_Dime_Out; Give_Merchandise = Give_Mechandise_Out; Give_Nickel = Give_Nickel_Out;
  //   NickelReceieved = NickelReceivedIn; QuarterReceieved = QuarterReceivedIn

  // Notes on the sheet:
  //   Nickel 5 cents
  //   Dime 10 cents
  //   Quarter 25 cents
endmodule

module Output (
  input  [3:0] CurrentState,
  input  [2:0] Coins,
  output [2:0] Output
);

  wire and_1_out, and_2_out, and_3_out, and_4_out, and_5_out, and_6_out, and_7_out, and_8_out, and_9_out,
       and_10_out, and_11_out, and_12_out, and_13_out, and_14_out, and_15_out, and_16_out, not_1_out,
       not_2_out, not_3_out, not_4_out, not_5_out, not_6_out;

  not not_1 (not_1_out, CurrentState[2]);
  not not_2 (not_2_out, CurrentState[1]);
  not not_3 (not_3_out, CurrentState[0]);
  not not_4 (not_4_out, Coins[2]);
  not not_5 (not_5_out, Coins[1]);
  not not_6 (not_6_out, Coins[0]);
  and and_1 (and_1_out, CurrentState[2], not_3_out, Coins[2], not_5_out, not_6_out);
  and and_2 (and_2_out, CurrentState[2], CurrentState[1], not_4_out, Coins[1], not_6_out);
  and and_3 (and_3_out, CurrentState[2], CurrentState[1], Coins[2], not_5_out, not_6_out);
  and and_4 (and_4_out, CurrentState[1], Coins[2], not_5_out, not_6_out);
  and and_5 (and_5_out, CurrentState[2], not_3_out, Coins[2], not_5_out, not_6_out);
  and and_6 (and_6_out, CurrentState[2], CurrentState[0], not_4_out, Coins[1], not_6_out);
  and and_7 (and_7_out, CurrentState[2], CurrentState[1], not_4_out, not_5_out, Coins[0]);
  and and_8 (and_8_out, CurrentState[2], CurrentState[1], not_4_out, Coins[1], not_6_out);
  and and_9 (and_9_out, CurrentState[2], CurrentState[1], CurrentState[0], not_4_out, not_5_out);
  and and_10 (and_10_out, not_1_out, CurrentState[0], Coins[2], not_5_out, not_6_out);
  and and_11 (and_11_out, CurrentState[2], not_3_out, not_4_out, Coins[1], not_6_out);
  and and_12 (and_12_out, CurrentState[2], not_3_out, Coins[2], not_5_out, not_6_out);
  and and_13 (and_13_out, CurrentState[2], not_2_out, CurrentState[0], not_4_out, not_5_out, Coins[0]);
  and and_14 (and_14_out, CurrentState[2], CurrentState[1], not_3_out, not_4_out, not_6_out);
  and and_15 (and_15_out, CurrentState[2], CurrentState[1], not_4_out, Coins[1], not_6_out);
  and and_16 (and_16_out, CurrentState[2], CurrentState[1], Coins[2], not_5_out, not_6_out);
  or or_1 (Output[2], and_1_out, and_2_out, and_3_out, CurrentState[3]);
  or or_2 (Output[1], and_4_out, and_5_out, and_6_out, and_7_out, and_8_out, and_9_out, CurrentState[3]);
  or or_3 (Output[0], and_10_out, and_11_out, and_12_out, and_13_out, and_14_out, and_15_out, and_16_out, CurrentState[3]);
endmodule
